# Fritzing sketch Diagram (saved by Fritzing 0.9.0b)
breadboards: 1

parts:
  Part2 = Arduino Ethernet Shield (Rev3)
  SW1 = PowerSwitch Tail II
  SW2 = PowerSwitch Tail II

nets:
  N1: Part2.SPI/D12, SW2.+in
  N2: Part2.SPI/D13, SW1.+in
  N3: Part2.GND, SW1.-in, SW1.Ground
  N4: SW2.-in, SW2.Ground
